# Fritzing sketch irremote-translator (saved by Fritzing 0.9.4)
breadboards: 1

parts:
  Part1 = Arduino Nano (Rev3.0) (ICSP)
  LED1 = LED - 5mm [color="Green (570nm)" package="5 mm [THT]"]
  IR1 = TSOP312.., 314.. [package=THT]
  LED6 = LED - 5mm [color="Red (660nm)" package="5 mm [THT]"]
  R5 = Resistor [tolerance=±5% resistance=470 package="0603 [SMD]"]
  R6 = Resistor [tolerance=±5% resistance=470 package="0603 [SMD]"]
  R7 = Resistor [tolerance=±5% resistance=470 package="0603 [SMD]"]
  S2 = Pushbutton [package="[SMD]"]
  U1 = TLP621 [package=THT]
  U2 = 3.5mm Audio Jack [package=audio-jack]
  R8 = Resistor [tolerance=±5% resistance=100 package="0603 [SMD]"]
  S3 = Pushbutton [package="[SMD]"]

nets:
  GND: Part1.GND, Part1.D11/MOSI, Part1.D12/MISO, IR1.GND, S2.Pin_3, S2.Pin_4, U2.SLEEVE, R8.Pin_1, S3.Pin_3, S3.Pin_4
  N1: Part1.D2, IR1.Data
  N2: Part1.D3, U1.Pin_1
  N3: Part1.D4, LED6.anode
  N4: Part1.D5, LED1.anode
  N5: Part1.5V, IR1.Vs, R5.Pin_0, R6.Pin_0, R7.Pin_1, U1.Pin_4
  N6: LED1.cathode, R6.Pin_1
  N7: LED6.cathode, R5.Pin_1
  N8: R7.Pin_0, U1.Pin_2
  N9: S2.Pin_1, S2.Pin_2
  N10: U1.Pin_3, U2.RIGHT, R8.Pin_0
  N11: S3.Pin_1, S3.Pin_2

notes:
  IR receiver, HW-447
  connected to D2
  LEDS:
  RED - status, connected to D4
  GREEN - storage, connected to D5
  3.5mm Audio Jack - used as input to amplifier IR receiver
  It is controlled by the optocoupler and D3
  Important note: IR input is high impedance and optocoupler has ~4-5us raise / fall time. 100 Ohm resistor allows signal to be still readable by the IR receiver
  Buttons (from left to right) -
  RECORD on D12 - initiates IRCode recording
  RESET on D11 - removes recorded codes
